# Fritzing sketch 09_DistanceDetector (saved by Fritzing 1.0.2b)
breadboards: 1

parts:
  Raspberry_Pi_1 = Raspberry Pi 3 [part_number=RPI-3-V1.2]
  HC-SR04_Sensor_1 = HC-SR04 Ultrasonic Distance Sensor

nets:
  N1: Raspberry_Pi_1.GPIO17, HC-SR04_Sensor_1.TRIG
  N2: Raspberry_Pi_1.GPIO22, HC-SR04_Sensor_1.ECHO
  GND: Raspberry_Pi_1.GND, HC-SR04_Sensor_1.GND
  5V: Raspberry_Pi_1.5V, HC-SR04_Sensor_1.VCC
