# Fritzing sketch 09_SoundDetector (saved by Fritzing 1.0.2b)
breadboards: 1

parts:
  Part1 = Arduino Uno (Rev3)
  Part2 = KY-037 High Sensitivity Sound Detection Module [package="Breakout board"]
  LED1 = smd LED [color="Red (633nm)" package="1206 [SMD]"]
  R1 = Resistor [tolerance=±5% resistance=220 package="0805 [SMD]"]

nets:
  N1: Part1.D8, Part2.D0
  N2: Part1.D13/SCK, LED1.anode
  N3: Part1.GND, Part2.G, R1.Pin_0
  N4: Part1.5V, Part2.+
  N5: LED1.cathode, R1.Pin_1

notes:
  +5V
  GND
  PIN13 (Toggle LED)
  PIN8 (Digital Trigger)

custom parts:
  KY-037 High Sensitivity Sound Detection Module: KY-037 high sensitivity sound detection module is an analog/digital sensor that uses a condenser microphone to observe changes in environment noise.
